# Fritzing sketch M6E_EthernetShield (saved by Fritzing 0.9.3b)
breadboards: 1

parts:
  Internet_Facing_Uno = Arduino Ethernet Shield (Rev3)
  SparkFun_Simultaneous_RFID_Reader_-_M6E_Nano1 = SparkFun Simultaneous RFID Reader - M6E Nano [part_number=SEN-14066]
  U1 = LIPO-1000mAh [package=lipo-1000]
  U2 = LIPO-1000mAh [package=lipo-1000]

nets:
  GND: Internet_Facing_Uno.GND, SparkFun_Simultaneous_RFID_Reader_-_M6E_Nano1.GND, U1.-, U2.-
  N1: Internet_Facing_Uno.D2, SparkFun_Simultaneous_RFID_Reader_-_M6E_Nano1.SOFT-RX
  N2: Internet_Facing_Uno.PWM_D3, SparkFun_Simultaneous_RFID_Reader_-_M6E_Nano1.SOFT-TX
  N3: SparkFun_Simultaneous_RFID_Reader_-_M6E_Nano1.N$12, U1.+, U2.+

custom parts:
  SparkFun Simultaneous RFID Reader - M6E Nano: Description: The SparkFun Simultaneous RFID Reader is an Arduino-compatible board to get you started with the M6E Nano UHF RFID Reader. Radio Frequency Identification (RFID) is becoming popular everywhere for tracking practically everything. Whether you want to get started by adding an RFID reader on your toolbox with tags on all your tools or allowing access to the tree house for your secret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
